# Fritzing sketch laser (saved by Fritzing 0.9.3b)
breadboards: 1

parts:
  Componente2 = Arduino Uno (Rev3)
  Q1 = PNP-Transistor [package="TO92 [THT]"]
  R1 = Photocell (LDR) [package=THT]
  LED1 = LED - 5mm [color="Yellow (595nm)" package="5 mm [THT]"]
  Componente3 = Humidity Sensor - HIH-4030 Breakout

nets:
  GND: Componente2.A0, Componente2.GND, R1.pin_1, Componente3.GND
  N1: Componente2.D4, LED1.anode
  N2: Componente2.D5_PWM, Q1.B, Componente3.VCC
  N3: Componente2.5V, Q1.E, R1.pin_0, LED1.cathode
  N4: Q1.C, Componente3.OUT
